# Fritzing sketch M0ModbusClimateControl (saved by Fritzing 1.0.0rc)
breadboards: 1

parts:
  Part2 = Adafruit Ethernet FeatherWing [part_number="Adafruit #3201"]
  Part3 = Adafruit SHT31-D Sensirion Temperature/Humidity Sensor [part_number="Adafruit #2857"]
  Part4 = Adafruit Feather M0 Basic Proto [part_number="Adafruit #2772"]
  LED1 = LED - 5mm [color="Red (633nm)" current=0.030A package="5 mm [THT]"]
  LED2 = LED - 5mm [color="Red (633nm)" current=0.030A package="5 mm [THT]"]
  LED3 = LED - 5mm [color="Red (633nm)" current=0.030A package="5 mm [THT]"]
  LED4 = LED - 5mm [color="Red (633nm)" current=0.030A package="5 mm [THT]"]
  R1 = Resistor [tolerance=±5% power=0.25W resistance=220 package=THT]
  R2 = Resistor [tolerance=±5% power=0.25W resistance=220 package=THT]
  R3 = Resistor [tolerance=±5% power=0.25W resistance=220 package=THT]
  R4 = Resistor [tolerance=±5% power=0.25W resistance=220 package=THT]

nets:
  3.3V: Part2.3.3V, Part3.VIN
  GND: Part2.GND, Part3.GND, Part4.GND, R1.Pin_1
  N1: Part2.F, Part4.SCK
  N2: Part2.MOSI, Part4.MOSI
  N3: Part2.MISO, Part4.MISO
  N4: Part2.K, Part4.D10
  N5: Part3.SCL, Part4.SCL
  N6: Part3.SDA, Part4.SDA
  N7: Part4.A3, LED4.cathode
  N8: Part4.A2, LED3.cathode
  N9: Part4.A1, LED2.cathode
  N10: Part4.A0, LED1.cathode
  N11: LED1.anode, R1.Pin_0
  N12: LED2.anode, R2.Pin_0
  N13: LED3.anode, R3.Pin_0
  N14: LED4.anode, R4.Pin_0
  N15: R2.Pin_1, R3.Pin_1, R4.Pin_1

custom parts:
  Adafruit Ethernet FeatherWing: Wireless is wonderful, but sometimes you want the strong reliability of a wire. If your Feather board is going to be part of a permanent installation, this Ethernet FeatherWing will let you add quick and easy wired Internet. Just plug in a standard ethernet cable, and run the Ethernet2 library for cross-platform networking. Ethernet is a tried-and-true networking standard. It's supported by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
  Adafruit SHT31-D Sensirion Temperature/Humidity Sensor: Sensirion Temperature/Humidity sensors are some of the finest & highest-accuracy devices you can get. And, finally we have some that have a true I2C interface for easy reading. The SHT31-D sensor has an excellent ±2% relative humidity and ±0.3°C accuracy for most uses. Unlike earlier SHT sensors, this sensor has a true I2C interface, and (bonus!) even with two address options. It also is 3V or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
  Adafruit Feather M0 Basic Proto: At the Feather M0's heart is an ATSAMD21G18 ARM Cortex M0 processor, clocked at 48 MHz and at 3.3V logic, the same one used in the new Arduino Zero. This chip has a whopping 256K of FLASH (8x more than the Atmega328 or 32u4) and 32K of RAM (16x as much)! This chip comes with built in USB so it has USB-to-Serial program & debug capability built in with no need for an FTDI-like chip. To make it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
